// Logisim project ex01.circ as structural Verilog: 1 circuit, main circuit main
module main (
  input  A,
  input  B,
  input  C,
  input  D,
  input  E,
  output S
);

  wire and_1_out, and_2_out;

  and and_1 (and_1_out, A, B, C, C);
  and and_2 (and_2_out, D, E);
  or or_1 (S, and_1_out, and_2_out);
endmodule
