// Logisim project ex02.circ as structural Verilog: 1 circuit, main circuit main
module main (
  input  A,
  input  B,
  input  C,
  input  D,
  input  E,
  input  A_2,
  input  B_2,
  input  C_2,
  input  D_2,
  input  E_2,
  output S,
  output S_2
);

  wire and_1_out, and_2_out, or_1_out, or_2_out;

  and and_1 (and_1_out, A, B, C);
  and and_2 (and_2_out, D, E);
  or or_1 (or_1_out, A_2, B_2, C_2);
  or or_2 (or_2_out, D_2, E_2);
  and and_3 (S, and_1_out, and_2_out);
  and and_4 (S_2, or_1_out, or_2_out);
endmodule
